// Logisim project 3_bit_up.circ as structural Verilog: 1 circuit, main circuit main
module main (
);

  wire clock_1_out, clock_2_out, clock_3_out, or_1_out, t_ff_1_q, t_ff_2_q, t_ff_3_q;

  Clock clock_1 (.out(clock_1_out));
  T_Flip_Flop t_ff_1 (.T(1'b1), .clk(clock_1_out), .Q(t_ff_1_q));  // open: Qn, reset, preset
  Clock clock_2 (.out(clock_2_out));
  LED led_1 (.in(t_ff_1_q));
  T_Flip_Flop t_ff_2 (.T(t_ff_1_q), .clk(clock_2_out), .Q(t_ff_2_q));  // open: Qn, reset, preset
  LED led_2 (.in(t_ff_2_q));
  Clock clock_3 (.out(clock_3_out));
  or or_1 (or_1_out, t_ff_1_q, t_ff_2_q);
  T_Flip_Flop t_ff_3 (.T(or_1_out), .clk(clock_3_out), .Q(t_ff_3_q));  // open: Qn, reset, preset
  LED led_3 (.in(t_ff_3_q));

  // Notes on the sheet:
  //   1
  //   2
  //   3
endmodule
