// Logisim project NowIts5Bitslol.circ as structural Verilog: 1 circuit, main circuit main
module main (
);

  wire and_1_out, and_2_out, and_3_out, button_1_out, clock_1_out, t_ff_1_q, t_ff_2_q, t_ff_3_q, t_ff_4_q,
       t_ff_5_q;

  Clock clock_1 (.out(clock_1_out));
  T_Flip_Flop t_ff_1 (.T(1'b1), .clk(clock_1_out), .Q(t_ff_1_q), .reset(button_1_out));  // open: Qn, preset
  Button button_1 (.out(button_1_out));
  LED led_1 (.in(t_ff_1_q));
  T_Flip_Flop t_ff_2 (.T(t_ff_1_q), .clk(clock_1_out), .Q(t_ff_2_q), .reset(button_1_out));  // open: Qn, preset
  LED led_2 (.in(t_ff_2_q));
  and and_1 (and_1_out, t_ff_1_q, t_ff_2_q);
  T_Flip_Flop t_ff_3 (.T(and_1_out), .clk(clock_1_out), .Q(t_ff_3_q), .reset(button_1_out));  // open: Qn, preset
  LED led_3 (.in(t_ff_3_q));
  and and_2 (and_2_out, t_ff_2_q, t_ff_3_q);
  T_Flip_Flop t_ff_4 (.T(and_2_out), .clk(clock_1_out), .Q(t_ff_4_q), .reset(button_1_out));  // open: Qn, preset
  LED led_4 (.in(t_ff_4_q));
  and and_3 (and_3_out, t_ff_3_q, t_ff_4_q);
  T_Flip_Flop t_ff_5 (.T(and_3_out), .clk(clock_1_out), .Q(t_ff_5_q), .reset(button_1_out));  // open: Qn, preset
  LED led_5 (.in(t_ff_5_q));

  // Notes on the sheet:
  //   1
  //   2
  //   3
endmodule
